// Logisim project stack_logisim.circ as structural Verilog: 25 circuits, main circuit totalizer
module stack (
  input  [1:0] COMMAND,
  input  CLOCK,
  input  RESET,
  input  [2:0] INDEX,
  input  [3:0] I_DATA,
  output [3:0] O_DATA
);

  wire and_1_out, commands_1_get, commands_1_pop, commands_1_push, demux_1_out_3, demux_1_out_4,
       demux_1_out_5, demux_1_out_6, demux_1_out_7;
  wire [2:0] number_1_addr;
  wire [3:0] mem_four_bit_1_out_data, mem_four_bit_2_out_data, mem_four_bit_3_out_data,
       mem_four_bit_4_out_data, mem_four_bit_5_out_data;

  commands commands_1 (.COMMAND(COMMAND), .PUSH(commands_1_push), .POP(commands_1_pop), .GET(commands_1_get));
  number number_1 (
    .PUSH(commands_1_push), .POP(commands_1_pop), .GET(commands_1_get), .CLK(CLOCK), .RESET(RESET),
    .INDEX(INDEX), .ADDR(number_1_addr));
  and and_1 (and_1_out, commands_1_push, CLOCK);
  demux demux_1 (
    .ADDR(number_1_addr), .in_2(and_1_out), .out_3(demux_1_out_3), .out_4(demux_1_out_4),
    .out_5(demux_1_out_5), .out_6(demux_1_out_6), .out_7(demux_1_out_7));
  mem_four_bit mem_four_bit_1 (.CLK(demux_1_out_3), .DATA(I_DATA), .RESET(RESET), .OUT_DATA(mem_four_bit_1_out_data));
  mem_four_bit mem_four_bit_2 (.CLK(demux_1_out_4), .DATA(I_DATA), .RESET(RESET), .OUT_DATA(mem_four_bit_2_out_data));
  mem_four_bit mem_four_bit_3 (.CLK(demux_1_out_5), .DATA(I_DATA), .RESET(RESET), .OUT_DATA(mem_four_bit_3_out_data));
  mem_four_bit mem_four_bit_4 (.CLK(demux_1_out_6), .DATA(I_DATA), .RESET(RESET), .OUT_DATA(mem_four_bit_4_out_data));
  mem_four_bit mem_four_bit_5 (.CLK(demux_1_out_7), .DATA(I_DATA), .RESET(RESET), .OUT_DATA(mem_four_bit_5_out_data));
  mux mux_1 (
    .ADDR(number_1_addr), .in_2(mem_four_bit_1_out_data), .in_3(mem_four_bit_2_out_data),
    .in_4(mem_four_bit_3_out_data), .in_5(mem_four_bit_4_out_data), .in_6(mem_four_bit_5_out_data), .Q(O_DATA));
endmodule

module number (
  input  PUSH,
  input  POP,
  input  GET,
  input  CLK,
  input  RESET,
  input  [2:0] INDEX,
  output [2:0] ADDR
);

  wire [2:0] and_1_out, and_2_out, and_3_out, get_pos_for_get_1_result, plus_one_1_out_2, totalizer_1_pointer;

  totalizer totalizer_1 (.CLK(CLK), .PUSH(PUSH), .POP(POP), .RESET(RESET), .POINTER(totalizer_1_pointer));
  plus_one plus_one_1 (.in_1(totalizer_1_pointer), .out_2(plus_one_1_out_2));
  get_pos_for_get get_pos_for_get_1 (.HEAD(totalizer_1_pointer), .INDEX(INDEX), .RESULT(get_pos_for_get_1_result));
  assign and_1_out = {3{PUSH}} & plus_one_1_out_2;  // AND_Gate and_1, 3 bits wide
  assign and_2_out = {3{POP}} & totalizer_1_pointer;  // AND_Gate and_2, 3 bits wide
  assign and_3_out = {3{GET}} & get_pos_for_get_1_result;  // AND_Gate and_3, 3 bits wide
  assign ADDR = and_1_out | and_2_out | and_3_out;  // OR_Gate or_1, 3 bits wide
endmodule

module totalizer (
  input  CLK,
  input  PUSH,
  input  POP,
  input  RESET,
  output [2:0] POINTER
);

  wire [2:0] and_1_out, and_2_out, change_number_1_out_2, change_number_1_out_3, or_1_out;

  assign and_1_out = change_number_1_out_2 & {3{PUSH}};  // AND_Gate and_1, 3 bits wide
  assign and_2_out = {3{POP}} & change_number_1_out_3;  // AND_Gate and_2, 3 bits wide
  assign or_1_out = and_1_out | and_2_out;  // OR_Gate or_1, 3 bits wide
  mem_3_bit mem_3_bit_1 (.DATA(or_1_out), .PUSH(PUSH), .POP(POP), .CLOCK(CLK), .RESET(RESET), .out_6(POINTER));
  change_number change_number_1 (.in_1(POINTER), .out_2(change_number_1_out_2), .out_3(change_number_1_out_3));
endmodule

module d_trigger (
  input  CLOCK,
  input  DATA,
  input  RESET,
  output out_4,
  output out_5
);

  wire and_1_out, not_1_out, not_2_out, or_1_out, or_2_out, sync_d_trigger_1_q;

  not not_1 (not_1_out, RESET);
  or or_1 (or_1_out, CLOCK, RESET);
  and and_1 (and_1_out, DATA, not_1_out);
  not not_2 (not_2_out, or_1_out);
  sync_d_trigger sync_d_trigger_1 (.C(or_1_out), .D(and_1_out), .Q(sync_d_trigger_1_q));  // open: notQ
  or or_2 (or_2_out, not_2_out, RESET);
  sync_d_trigger sync_d_trigger_2 (.C(or_2_out), .D(sync_d_trigger_1_q), .Q(out_4), .notQ(out_5));
endmodule

module mem_3_bit (
  input  [2:0] DATA,
  input  PUSH,
  input  POP,
  input  CLOCK,
  input  RESET,
  output [2:0] out_6
);

  wire and_1_out, and_2_out, xor_1_out;

  and and_1 (and_1_out, POP, CLOCK);
  and and_2 (and_2_out, PUSH, CLOCK);
  xor xor_1 (xor_1_out, and_2_out, and_1_out);
  d_trigger d_trigger_1 (.CLOCK(xor_1_out), .DATA(DATA[0]), .RESET(RESET), .out_4(out_6[0]));  // open: out_5
  d_trigger d_trigger_2 (.CLOCK(xor_1_out), .DATA(DATA[1]), .RESET(RESET), .out_4(out_6[1]));  // open: out_5
  d_trigger d_trigger_3 (.CLOCK(xor_1_out), .DATA(DATA[2]), .RESET(RESET), .out_4(out_6[2]));  // open: out_5
endmodule

module plus_one (
  input  [2:0] in_1,
  output [2:0] out_2
);

  wire [2:0] addition_1_out_3, by_module_5_1_out_2;

  by_module_5 by_module_5_1 (.in_1(in_1), .out_2(by_module_5_1_out_2));
  addition addition_1 (.in_1(by_module_5_1_out_2), .in_2(3'b001), .out_3(addition_1_out_3));
  by_module_5 by_module_5_2 (.in_1(addition_1_out_3), .out_2(out_2));
endmodule

module change_number (
  input  [2:0] in_1,
  output [2:0] out_2,
  output [2:0] out_3
);

  get_pos_for_get get_pos_for_get_1 (.HEAD(in_1), .INDEX(3'b001), .RESULT(out_3));
  plus_one plus_one_1 (.in_1(in_1), .out_2(out_2));
endmodule

module get_pos_for_get (
  input  [2:0] HEAD,
  input  [2:0] INDEX,
  output [2:0] RESULT
);

  wire [2:0] addition_1_out_3, and_1_out, and_2_out, by_module_5_1_out_2, by_module_5_2_out_2, or_1_out,
       subtraction_1_out_3, subtraction_2_out_3;
  wire [2:2] comp_1_out_3, comp_1_out_4;

  by_module_5 by_module_5_1 (.in_1(HEAD), .out_2(by_module_5_1_out_2));
  by_module_5 by_module_5_2 (.in_1(INDEX), .out_2(by_module_5_2_out_2));
  comp comp_1 (.A(by_module_5_1_out_2), .B(by_module_5_2_out_2), .out_3(comp_1_out_3[2]), .out_4(comp_1_out_4[2]));
  subtraction subtraction_1 (.in_1(by_module_5_1_out_2), .in_2(by_module_5_2_out_2), .out_3(subtraction_1_out_3));
  subtraction subtraction_2 (.in_1(3'b101), .in_2(by_module_5_2_out_2), .out_3(subtraction_2_out_3));
  addition addition_1 (.in_1(by_module_5_1_out_2), .in_2(subtraction_2_out_3), .out_3(addition_1_out_3));
  assign and_1_out = {3{comp_1_out_3[2]}} & subtraction_1_out_3;  // AND_Gate and_1, 3 bits wide
  assign and_2_out = addition_1_out_3 & {3{comp_1_out_4[2]}};  // AND_Gate and_2, 3 bits wide
  assign or_1_out = and_1_out | and_2_out;  // OR_Gate or_1, 3 bits wide
  by_module_5 by_module_5_3 (.in_1(or_1_out), .out_2(RESULT));
endmodule

module summator (
  input  in_1,
  input  in_2,
  input  OST,
  output SUM,
  output OST_AFTER
);

  wire and_1_out, and_2_out, xor_1_out;

  xor xor_1 (xor_1_out, in_1, in_2);
  and and_1 (and_1_out, in_1, in_2);
  and and_2 (and_2_out, xor_1_out, OST);
  xor xor_2 (OST_AFTER, and_2_out, and_1_out);
  xor xor_3 (SUM, xor_1_out, OST);
endmodule

module comp (
  input  [2:0] A,
  input  [2:0] B,
  output out_3,
  output out_4
);

  wire and_1_out, and_2_out, eq_1_out_3, eq_2_out_3, eq_3_out_3, greater_1_out_3, greater_2_out_3,
       greater_3_out_3, or_1_out, or_2_out;

  eq eq_1 (.in_1(A[0]), .in_2(B[0]), .out_3(eq_1_out_3));
  greater greater_1 (.in_1(A[0]), .in_2(B[0]), .out_3(greater_1_out_3));
  or or_1 (or_1_out, eq_1_out_3, greater_1_out_3);
  eq eq_2 (.in_1(A[1]), .in_2(B[1]), .out_3(eq_2_out_3));
  greater greater_2 (.in_1(A[1]), .in_2(B[1]), .out_3(greater_2_out_3));
  and and_1 (and_1_out, or_1_out, eq_2_out_3);
  eq eq_3 (.in_1(A[2]), .in_2(B[2]), .out_3(eq_3_out_3));
  greater greater_3 (.in_1(A[2]), .in_2(B[2]), .out_3(greater_3_out_3));
  or or_2 (or_2_out, and_1_out, greater_2_out_3);
  and and_2 (and_2_out, or_2_out, eq_3_out_3);
  or or_3 (out_3, and_2_out, greater_3_out_3);
  not not_1 (out_4, out_3);
endmodule

module five_to_three (
  input  in_1,
  input  in_2,
  input  in_3,
  input  in_4,
  input  in_5,
  output [2:0] out_6
);

  or or_1 (out_6[0], in_2, in_4);
  or or_2 (out_6[1], in_3, in_4);

  assign out_6[2] = in_5;
endmodule

module subtraction (
  input  [2:0] in_1,
  input  [2:0] in_2,
  output [2:0] out_3
);

  wire summator_1_ost_after, summator_2_ost_after;
  wire [2:0] not_1_out;

  assign not_1_out = ~in_2;  // NOT_Gate not_1, 3 bits wide
  summator summator_1 (
    .in_1(in_1[0]), .in_2(not_1_out[0]), .OST(1'b1), .SUM(out_3[0]), .OST_AFTER(summator_1_ost_after));
  summator summator_2 (
    .in_1(in_1[1]), .in_2(not_1_out[1]), .OST(summator_1_ost_after), .SUM(out_3[1]),
    .OST_AFTER(summator_2_ost_after));
  summator summator_3 (
    .in_1(in_1[2]), .in_2(not_1_out[2]), .OST(summator_2_ost_after), .SUM(out_3[2]));  // open: OST_AFTER
endmodule

module addition (
  input  [2:0] in_1,
  input  [2:0] in_2,
  output [2:0] out_3
);

  wire summator_1_ost_after, summator_2_ost_after;

  summator summator_1 (.in_1(in_1[0]), .in_2(in_2[0]), .OST(1'b0), .SUM(out_3[0]), .OST_AFTER(summator_1_ost_after));
  summator summator_2 (
    .in_1(in_1[1]), .in_2(in_2[1]), .OST(summator_1_ost_after), .SUM(out_3[1]),
    .OST_AFTER(summator_2_ost_after));
  summator summator_3 (.in_1(in_1[2]), .in_2(in_2[2]), .OST(summator_2_ost_after), .SUM(out_3[2]));  // open: OST_AFTER
endmodule

module main (
  input  CLK,
  input  RESET,
  input  [1:0] COMMAND,
  input  [2:0] INDEX,
  input  [3:0] IDATA,
  output [3:0] ODATA
);

  stack stack_1 (.COMMAND(COMMAND), .CLOCK(CLK), .RESET(RESET), .INDEX(INDEX), .I_DATA(IDATA), .O_DATA(ODATA));
endmodule

module commands (
  input  [1:0] COMMAND,
  output PUSH,
  output POP,
  output GET
);

  wire not_1_out, not_2_out;

  and and_1 (PUSH, COMMAND[0], not_1_out);
  not not_1 (not_1_out, COMMAND[1]);
  not not_2 (not_2_out, COMMAND[0]);
  and and_2 (POP, not_2_out, COMMAND[1]);
  and and_3 (GET, COMMAND[0], COMMAND[1]);
endmodule

module three_to_five (
  input  in_1,
  input  in_2,
  input  in_3,
  output out_4,
  output out_5,
  output out_6,
  output out_7,
  output out_8
);

  wire and_1_out, and_2_out, and_3_out, and_4_out, and_5_out, and_6_out, and_7_out, and_8_out, and_9_out,
       and_10_out, and_11_out, and_14_out, and_15_out, and_16_out, not_1_out, not_2_out, not_3_out;

  not not_1 (not_1_out, in_3);
  not not_2 (not_2_out, in_2);
  not not_3 (not_3_out, in_1);
  and and_1 (and_1_out, not_3_out, not_2_out);
  and and_2 (and_2_out, in_1, not_2_out);
  and and_3 (and_3_out, not_3_out, in_2);
  and and_4 (and_4_out, in_1, in_2);
  and and_5 (and_5_out, not_3_out, not_2_out);
  and and_6 (and_6_out, in_1, not_2_out);
  and and_7 (and_7_out, not_3_out, in_2);
  and and_8 (and_8_out, in_1, in_2);
  and and_9 (and_9_out, not_1_out, and_1_out);
  and and_10 (and_10_out, not_1_out, and_2_out);
  and and_11 (and_11_out, not_1_out, and_3_out);
  and and_12 (out_7, not_1_out, and_4_out);
  and and_13 (out_8, in_3, and_5_out);
  and and_14 (and_14_out, in_3, and_6_out);
  and and_15 (and_15_out, in_3, and_7_out);
  and and_16 (and_16_out, in_3, and_8_out);
  or or_1 (out_4, and_9_out, and_14_out);
  or or_2 (out_5, and_10_out, and_15_out);
  or or_3 (out_6, and_11_out, and_16_out);
endmodule

module mux (
  input  [2:0] ADDR,
  input  [3:0] in_2,
  input  [3:0] in_3,
  input  [3:0] in_4,
  input  [3:0] in_5,
  input  [3:0] in_6,
  output [3:0] Q
);

  wire [3:0] and_1_out, and_2_out, and_3_out, and_4_out, and_5_out, or_1_out, or_2_out, or_3_out;
  wire [3:3] three_to_five_1_out_4, three_to_five_1_out_5, three_to_five_1_out_6, three_to_five_1_out_7,
       three_to_five_1_out_8;

  three_to_five three_to_five_1 (
    .in_1(ADDR[0]), .in_2(ADDR[1]), .in_3(ADDR[2]), .out_4(three_to_five_1_out_4[3]),
    .out_5(three_to_five_1_out_5[3]), .out_6(three_to_five_1_out_6[3]), .out_7(three_to_five_1_out_7[3]),
    .out_8(three_to_five_1_out_8[3]));
  assign and_1_out = {4{three_to_five_1_out_4[3]}} & in_2;  // AND_Gate and_1, 4 bits wide
  assign and_2_out = {4{three_to_five_1_out_5[3]}} & in_3;  // AND_Gate and_2, 4 bits wide
  assign and_3_out = {4{three_to_five_1_out_6[3]}} & in_4;  // AND_Gate and_3, 4 bits wide
  assign and_4_out = {4{three_to_five_1_out_7[3]}} & in_5;  // AND_Gate and_4, 4 bits wide
  assign and_5_out = {4{three_to_five_1_out_8[3]}} & in_6;  // AND_Gate and_5, 4 bits wide
  assign or_1_out = and_1_out | and_2_out;  // OR_Gate or_1, 4 bits wide
  assign or_2_out = and_3_out | and_4_out;  // OR_Gate or_2, 4 bits wide
  assign or_3_out = or_2_out | and_5_out;  // OR_Gate or_3, 4 bits wide
  assign Q = or_1_out | or_3_out;  // OR_Gate or_4, 4 bits wide
endmodule

module demux (
  input  [2:0] ADDR,
  input  in_2,
  output out_3,
  output out_4,
  output out_5,
  output out_6,
  output out_7
);

  wire three_to_five_1_out_4, three_to_five_1_out_5, three_to_five_1_out_6, three_to_five_1_out_7,
       three_to_five_1_out_8;

  three_to_five three_to_five_1 (
    .in_1(ADDR[0]), .in_2(ADDR[1]), .in_3(ADDR[2]), .out_4(three_to_five_1_out_4),
    .out_5(three_to_five_1_out_5), .out_6(three_to_five_1_out_6), .out_7(three_to_five_1_out_7),
    .out_8(three_to_five_1_out_8));
  and and_1 (out_3, three_to_five_1_out_4, in_2);
  and and_2 (out_4, three_to_five_1_out_5, in_2);
  and and_3 (out_5, three_to_five_1_out_6, in_2);
  and and_4 (out_6, three_to_five_1_out_7, in_2);
  and and_5 (out_7, three_to_five_1_out_8, in_2);
endmodule

module sync_d_trigger (
  input  C,
  input  D,
  output Q,
  output notQ
);

  wire not_1_out;

  not not_1 (not_1_out, D);
  rs_trigger rs_trigger_1 (.R(not_1_out), .C(C), .S(D), .Q(Q), .notQ(notQ));
endmodule

module mem_four_bit (
  input  CLK,
  input  [3:0] DATA,
  input  RESET,
  output [3:0] OUT_DATA
);

  d_trigger_reset d_trigger_reset_1 (.CLK(CLK), .DATA(DATA[0]), .RESET(RESET), .Q(OUT_DATA[0]));  // open: notQ
  d_trigger_reset d_trigger_reset_2 (.CLK(CLK), .DATA(DATA[1]), .RESET(RESET), .Q(OUT_DATA[1]));  // open: notQ
  d_trigger_reset d_trigger_reset_3 (.CLK(CLK), .DATA(DATA[2]), .RESET(RESET), .Q(OUT_DATA[2]));  // open: notQ
  d_trigger_reset d_trigger_reset_4 (.CLK(CLK), .DATA(DATA[3]), .RESET(RESET), .Q(OUT_DATA[3]));  // open: notQ
endmodule

module rs_trigger (
  input  R,
  input  C,
  input  S,
  output Q,
  output notQ
);

  wire and_1_out, and_2_out;

  and and_1 (and_1_out, R, C);
  and and_2 (and_2_out, C, S);
  nor nor_1 (Q, and_1_out, notQ);
  nor nor_2 (notQ, Q, and_2_out);
endmodule

module d_trigger_reset (
  input  CLK,
  input  DATA,
  input  RESET,
  output Q,
  output notQ
);

  wire and_1_out, not_1_out, or_1_out;

  not not_1 (not_1_out, RESET);
  or or_1 (or_1_out, CLK, RESET);
  and and_1 (and_1_out, DATA, not_1_out);
  sync_d_trigger sync_d_trigger_1 (.C(or_1_out), .D(and_1_out), .Q(Q), .notQ(notQ));
endmodule

module by_module_5 (
  input  [2:0] in_1,
  output [2:0] out_2
);

  wire three_to_five_1_out_4, three_to_five_1_out_5, three_to_five_1_out_6, three_to_five_1_out_7,
       three_to_five_1_out_8;

  three_to_five three_to_five_1 (
    .in_1(in_1[0]), .in_2(in_1[1]), .in_3(in_1[2]), .out_4(three_to_five_1_out_4),
    .out_5(three_to_five_1_out_5), .out_6(three_to_five_1_out_6), .out_7(three_to_five_1_out_7),
    .out_8(three_to_five_1_out_8));
  five_to_three five_to_three_1 (
    .in_1(three_to_five_1_out_4), .in_2(three_to_five_1_out_5), .in_3(three_to_five_1_out_6),
    .in_4(three_to_five_1_out_7), .in_5(three_to_five_1_out_8), .out_6(out_2));
endmodule

module eq (
  input  in_1,
  input  in_2,
  output out_3
);

  wire xor_1_out;

  xor xor_1 (xor_1_out, in_1, in_2);
  not not_1 (out_3, xor_1_out);
endmodule

module greater (
  input  in_1,
  input  in_2,
  output out_3
);

  wire not_1_out;

  not not_1 (not_1_out, in_2);
  and and_1 (out_3, in_1, not_1_out);
endmodule
